// Logisim project alu.circ as structural Verilog: 6 circuits, main circuit 2-bit-adder
module _2_bit_adder (
  input  [1:0] a,
  input  [1:0] b,
  output [1:0] sum,
  output carry_out
);

  wire half_adder_1_carry;

  half_adder half_adder_1 (.a(a[0]), .b(b[0]), .sum(sum[0]), .carry(half_adder_1_carry));
  full_adder full_adder_1 (.carry_in(half_adder_1_carry), .a(a[1]), .b(b[1]), .sum(sum[1]), .carry_out(carry_out));
endmodule

module half_adder (
  input  a,
  input  b,
  output sum,
  output carry
);

  \xor  xor_1 (.a(a), .b(b), .out_3(sum));
  \and  and_1 (.a(b), .b(a), .out(carry));
endmodule

module full_adder (
  input  carry_in,
  input  a,
  input  b,
  output sum,
  output carry_out
);

  wire half_adder_1_carry, half_adder_2_carry, half_adder_2_sum;

  half_adder half_adder_1 (.a(carry_in), .b(half_adder_2_sum), .sum(sum), .carry(half_adder_1_carry));
  half_adder half_adder_2 (.a(a), .b(b), .sum(half_adder_2_sum), .carry(half_adder_2_carry));
  \or  or_1 (.a(half_adder_1_carry), .b(half_adder_2_carry), .out(carry_out));
endmodule

module _8_bit_adder (
  input  [7:0] in_1,
  input  [7:0] in_2,
  output [7:0] out_3,
  output carry_out
);

  wire full_adder_1_carry_out, full_adder_2_carry_out, full_adder_3_carry_out, full_adder_4_carry_out,
       full_adder_5_carry_out, full_adder_6_carry_out, half_adder_1_carry;

  half_adder half_adder_1 (.a(in_1[0]), .b(in_2[0]), .sum(out_3[0]), .carry(half_adder_1_carry));
  full_adder full_adder_1 (
    .carry_in(half_adder_1_carry), .a(in_1[1]), .b(in_2[1]), .sum(out_3[1]),
    .carry_out(full_adder_1_carry_out));
  full_adder full_adder_2 (
    .carry_in(full_adder_1_carry_out), .a(in_1[2]), .b(in_2[2]), .sum(out_3[2]),
    .carry_out(full_adder_2_carry_out));
  full_adder full_adder_3 (
    .carry_in(full_adder_2_carry_out), .a(in_1[3]), .b(in_2[3]), .sum(out_3[3]),
    .carry_out(full_adder_3_carry_out));
  full_adder full_adder_4 (
    .carry_in(full_adder_3_carry_out), .a(in_1[4]), .b(in_2[4]), .sum(out_3[4]),
    .carry_out(full_adder_4_carry_out));
  full_adder full_adder_5 (
    .carry_in(full_adder_4_carry_out), .a(in_1[5]), .b(in_2[5]), .sum(out_3[5]),
    .carry_out(full_adder_5_carry_out));
  full_adder full_adder_6 (
    .carry_in(full_adder_5_carry_out), .a(in_1[6]), .b(in_2[6]), .sum(out_3[6]),
    .carry_out(full_adder_6_carry_out));
  full_adder full_adder_7 (
    .carry_in(full_adder_6_carry_out), .a(in_1[7]), .b(in_2[7]), .sum(out_3[7]), .carry_out(carry_out));
endmodule

module _4_bit_adder (
  input  [3:0] in_1,
  input  [3:0] in_2,
  output [3:0] out_3,
  output carry_out
);

  wire full_adder_1_carry_out, full_adder_2_carry_out, half_adder_1_carry;

  half_adder half_adder_1 (.a(in_1[0]), .b(in_2[0]), .sum(out_3[0]), .carry(half_adder_1_carry));
  full_adder full_adder_1 (
    .carry_in(half_adder_1_carry), .a(in_1[1]), .b(in_2[1]), .sum(out_3[1]),
    .carry_out(full_adder_1_carry_out));
  full_adder full_adder_2 (
    .carry_in(full_adder_1_carry_out), .a(in_1[2]), .b(in_2[2]), .sum(out_3[2]),
    .carry_out(full_adder_2_carry_out));
  full_adder full_adder_3 (
    .carry_in(full_adder_2_carry_out), .a(in_1[3]), .b(in_2[3]), .sum(out_3[3]), .carry_out(carry_out));
endmodule

module _4_bit_inc (
  input  [3:0] \input ,
  output [3:0] sum,
  output carry_out
);

  wire half_adder_1_carry, half_adder_2_carry;

  \not  not_1 (.\input (\input [0]), .\output (sum[0]));
  half_adder half_adder_1 (.a(\input [0]), .b(\input [1]), .sum(sum[1]), .carry(half_adder_1_carry));
  half_adder half_adder_2 (.a(half_adder_1_carry), .b(\input [2]), .sum(sum[2]), .carry(half_adder_2_carry));
  half_adder half_adder_3 (.a(half_adder_2_carry), .b(\input [3]), .sum(sum[3]), .carry(carry_out));
endmodule
