// Logisim project combinatorial-logic.circ as structural Verilog: 7 circuits, main circuit 2:1_1-bit_mux
module _2_1_1_bit_mux (
  input  a,
  input  sel,
  input  b,
  output out
);

  wire and_1_out, and_2_out, undriven;

  \and  and_1 (.a(a), .b(undriven), .out(and_1_out));
  \or  or_1 (.a(and_1_out), .b(and_2_out), .out(out));
  \and  and_2 (.a(sel), .b(b), .out(and_2_out));
endmodule

module _1_2_1_bit_mux (
  input  out,
  input  sel,
  output a,
  output b
);

  wire undriven;

  \and  and_1 (.a(out), .b(undriven), .out(a));
  \and  and_2 (.a(sel), .b(out), .out(b));
endmodule

module _2_4_decoder (
  input  [1:0] idx,
  output idx_0,
  output idx_1,
  output idx_2,
  output idx_3
);

  wire not_1_output, not_2_output;

  \not  not_1 (.\input (idx[0]), .\output (not_1_output));
  \not  not_2 (.\input (idx[1]), .\output (not_2_output));
  \and  and_1 (.a(not_1_output), .b(not_2_output), .out(idx_0));
  \and  and_2 (.a(idx[0]), .b(not_2_output), .out(idx_1));
  \and  and_3 (.a(not_1_output), .b(idx[1]), .out(idx_2));
  \and  and_4 (.a(idx[0]), .b(idx[1]), .out(idx_3));

  // Notes on the sheet:
  //   2-bit address
  //   address decode logic
  //   2^2=4 addresses
endmodule

module _4_1_4_bit_mux (
  input  [1:0] idx,
  input  [3:0] in_0,
  input  [3:0] in_1,
  input  [3:0] in_2,
  input  [3:0] in_3,
  output [3:0] out
);

  wire and_1_out, and_2_out, and_3_out, and_4_out, and_5_out, and_6_out, and_7_out, and_8_out, and_9_out,
       and_10_out, and_11_out, and_12_out, and_13_out, and_14_out, and_15_out, and_16_out,
       n2_4_decoder_1_idx_0, n2_4_decoder_1_idx_1, n2_4_decoder_1_idx_2, n2_4_decoder_1_idx_3, or_1_out,
       or_2_out, or_3_out, or_4_out, or_6_out, or_8_out, or_10_out, or_11_out;

  _2_4_decoder u_2_4_decoder_1 (
    .idx(idx), .idx_0(n2_4_decoder_1_idx_0), .idx_1(n2_4_decoder_1_idx_1), .idx_2(n2_4_decoder_1_idx_2),
    .idx_3(n2_4_decoder_1_idx_3));
  \and  and_1 (.a(n2_4_decoder_1_idx_0), .b(in_0[0]), .out(and_1_out));
  \and  and_2 (.a(n2_4_decoder_1_idx_0), .b(in_0[1]), .out(and_2_out));
  \and  and_3 (.a(n2_4_decoder_1_idx_1), .b(in_1[0]), .out(and_3_out));
  \and  and_4 (.a(n2_4_decoder_1_idx_1), .b(in_1[1]), .out(and_4_out));
  \and  and_5 (.a(n2_4_decoder_1_idx_2), .b(in_2[0]), .out(and_5_out));
  \and  and_6 (.a(n2_4_decoder_1_idx_2), .b(in_2[1]), .out(and_6_out));
  \and  and_7 (.a(n2_4_decoder_1_idx_3), .b(in_3[0]), .out(and_7_out));
  \and  and_8 (.a(n2_4_decoder_1_idx_3), .b(in_3[1]), .out(and_8_out));
  \and  and_9 (.a(n2_4_decoder_1_idx_0), .b(in_0[2]), .out(and_9_out));
  \and  and_10 (.a(n2_4_decoder_1_idx_0), .b(in_0[3]), .out(and_10_out));
  \and  and_11 (.a(n2_4_decoder_1_idx_1), .b(in_1[2]), .out(and_11_out));
  \and  and_12 (.a(n2_4_decoder_1_idx_1), .b(in_1[3]), .out(and_12_out));
  \and  and_13 (.a(n2_4_decoder_1_idx_2), .b(in_2[2]), .out(and_13_out));
  \and  and_14 (.a(n2_4_decoder_1_idx_2), .b(in_2[3]), .out(and_14_out));
  \and  and_15 (.a(n2_4_decoder_1_idx_3), .b(in_3[2]), .out(and_15_out));
  \and  and_16 (.a(n2_4_decoder_1_idx_3), .b(in_3[3]), .out(and_16_out));
  \or  or_1 (.a(and_1_out), .b(and_3_out), .out(or_1_out));
  \or  or_2 (.a(and_2_out), .b(and_4_out), .out(or_2_out));
  \or  or_3 (.a(and_9_out), .b(and_11_out), .out(or_3_out));
  \or  or_4 (.a(or_1_out), .b(and_5_out), .out(or_4_out));
  \or  or_5 (.a(or_4_out), .b(and_7_out), .out(out[0]));
  \or  or_6 (.a(or_2_out), .b(and_6_out), .out(or_6_out));
  \or  or_7 (.a(or_6_out), .b(and_8_out), .out(out[1]));
  \or  or_8 (.a(or_3_out), .b(and_13_out), .out(or_8_out));
  \or  or_9 (.a(or_8_out), .b(and_15_out), .out(out[2]));
  \or  or_10 (.a(and_10_out), .b(and_12_out), .out(or_10_out));
  \or  or_11 (.a(or_10_out), .b(and_14_out), .out(or_11_out));
  \or  or_12 (.a(or_11_out), .b(and_16_out), .out(out[3]));

  // Notes on the sheet:
  //   2-bit address (4 inputs max)
  //   4 inputs, each 4-bit
  //   bitwise AND
  //   for all i: out |= idx[i] & in[i]
  //   bitwise OR
  //   LOGIC: if idx==i: out=in[i]
  //   1 output, 4-bit
endmodule

module _1_4_4_bit_mux (
  input  [1:0] idx,
  input  [3:0] in,
  output [3:0] out_0,
  output [3:0] out_1,
  output [3:0] out_2,
  output [3:0] out_3
);

  wire n2_4_decoder_1_idx_0, n2_4_decoder_1_idx_1, n2_4_decoder_1_idx_2, n2_4_decoder_1_idx_3;

  _2_4_decoder u_2_4_decoder_1 (
    .idx(idx), .idx_0(n2_4_decoder_1_idx_0), .idx_1(n2_4_decoder_1_idx_1), .idx_2(n2_4_decoder_1_idx_2),
    .idx_3(n2_4_decoder_1_idx_3));
  \and  and_1 (.a(n2_4_decoder_1_idx_0), .b(in[0]), .out(out_0[0]));
  \and  and_2 (.a(n2_4_decoder_1_idx_0), .b(in[1]), .out(out_0[1]));
  \and  and_3 (.a(n2_4_decoder_1_idx_0), .b(in[2]), .out(out_0[2]));
  \and  and_4 (.a(n2_4_decoder_1_idx_0), .b(in[3]), .out(out_0[3]));
  \and  and_5 (.a(n2_4_decoder_1_idx_1), .b(in[0]), .out(out_1[0]));
  \and  and_6 (.a(n2_4_decoder_1_idx_1), .b(in[1]), .out(out_1[1]));
  \and  and_7 (.a(n2_4_decoder_1_idx_1), .b(in[2]), .out(out_1[2]));
  \and  and_8 (.a(n2_4_decoder_1_idx_1), .b(in[3]), .out(out_1[3]));
  \and  and_9 (.a(n2_4_decoder_1_idx_2), .b(in[0]), .out(out_2[0]));
  \and  and_10 (.a(n2_4_decoder_1_idx_2), .b(in[1]), .out(out_2[1]));
  \and  and_11 (.a(n2_4_decoder_1_idx_2), .b(in[2]), .out(out_2[2]));
  \and  and_12 (.a(n2_4_decoder_1_idx_2), .b(in[3]), .out(out_2[3]));
  \and  and_13 (.a(n2_4_decoder_1_idx_3), .b(in[0]), .out(out_3[0]));
  \and  and_14 (.a(n2_4_decoder_1_idx_3), .b(in[1]), .out(out_3[1]));
  \and  and_15 (.a(n2_4_decoder_1_idx_3), .b(in[2]), .out(out_3[2]));
  \and  and_16 (.a(n2_4_decoder_1_idx_3), .b(in[3]), .out(out_3[3]));

  // Notes on the sheet:
  //   2-bit address (4 inputs max)
  //   4-bit input
  //   LOGIC: for all i: out[i] = idx[i] & in
  //   idx[i] & (in>>i)
  //   4 4-bit outputs
endmodule

module _1_4_1_bit_mux (
  input  [1:0] idx,
  input  in,
  output out_0,
  output out_1,
  output out_2,
  output out_3
);

  wire n2_4_decoder_1_idx_0, n2_4_decoder_1_idx_1, n2_4_decoder_1_idx_2, n2_4_decoder_1_idx_3;

  _2_4_decoder u_2_4_decoder_1 (
    .idx(idx), .idx_0(n2_4_decoder_1_idx_0), .idx_1(n2_4_decoder_1_idx_1), .idx_2(n2_4_decoder_1_idx_2),
    .idx_3(n2_4_decoder_1_idx_3));
  \and  and_1 (.a(n2_4_decoder_1_idx_0), .b(in), .out(out_0));
  \and  and_2 (.a(n2_4_decoder_1_idx_1), .b(in), .out(out_1));
  \and  and_3 (.a(n2_4_decoder_1_idx_2), .b(in), .out(out_2));
  \and  and_4 (.a(n2_4_decoder_1_idx_3), .b(in), .out(out_3));

  // Notes on the sheet:
  //   2-bit address (4 inputs max)
  //   1-bit input
  //   LOGIC: for all i: out[i] = idx[i] & in
  //   idx[i] & in
  //   4 1-bit outputs
endmodule

module _2_1_4_bit_mux (
  input  idx,
  input  [3:0] in_0,
  input  [3:0] in_1,
  output [3:0] out
);

  wire and_1_out, and_2_out, and_3_out, and_4_out, and_5_out, and_6_out, and_7_out, and_8_out, not_1_output;

  \not  not_1 (.\input (idx), .\output (not_1_output));
  \and  and_1 (.a(not_1_output), .b(in_0[0]), .out(and_1_out));
  \and  and_2 (.a(not_1_output), .b(in_0[1]), .out(and_2_out));
  \and  and_3 (.a(not_1_output), .b(in_0[2]), .out(and_3_out));
  \and  and_4 (.a(not_1_output), .b(in_0[3]), .out(and_4_out));
  \and  and_5 (.a(idx), .b(in_1[0]), .out(and_5_out));
  \and  and_6 (.a(idx), .b(in_1[1]), .out(and_6_out));
  \and  and_7 (.a(idx), .b(in_1[2]), .out(and_7_out));
  \and  and_8 (.a(idx), .b(in_1[3]), .out(and_8_out));
  \or  or_1 (.a(and_1_out), .b(and_5_out), .out(out[0]));
  \or  or_2 (.a(and_2_out), .b(and_6_out), .out(out[1]));
  \or  or_3 (.a(and_3_out), .b(and_7_out), .out(out[2]));
  \or  or_4 (.a(and_4_out), .b(and_8_out), .out(out[3]));
endmodule
