// Logisim project sequential-logic.circ as structural Verilog: 7 circuits, main circuit rs-latch
module rs_latch (
  input  r,
  input  s,
  output out,
  output not_out
);

  \nor  nor_1 (.a(r), .b(not_out), .out(out));
  \nor  nor_2 (.a(out), .b(s), .out(not_out));
endmodule

module d_latch (
  input  in,
  input  load,
  output out,
  output not_out
);

  wire and_1_out, and_2_out, not_1_output;

  \not  not_1 (.\input (in), .\output (not_1_output));
  \and  and_1 (.a(not_1_output), .b(load), .out(and_1_out));
  \and  and_2 (.a(in), .b(load), .out(and_2_out));
  rs_latch rs_latch_1 (.r(and_1_out), .s(and_2_out), .out(out), .not_out(not_out));

  // Notes on the sheet:
  //   reset
  //   set
endmodule

module _8_bit_reg (
  input  clk,
  input  wr,
  input  [7:0] in,
  output [7:0] out
);

  wire and_1_out;

  \and  and_1 (.a(clk), .b(wr), .out(and_1_out));
  d_latch d_latch_1 (.in(in[0]), .load(and_1_out), .out(out[0]));  // open: not_out
  d_latch d_latch_2 (.in(in[1]), .load(and_1_out), .out(out[1]));  // open: not_out
  d_latch d_latch_3 (.in(in[2]), .load(and_1_out), .out(out[2]));  // open: not_out
  d_latch d_latch_4 (.in(in[3]), .load(and_1_out), .out(out[3]));  // open: not_out
  d_latch d_latch_5 (.in(in[4]), .load(and_1_out), .out(out[4]));  // open: not_out
  d_latch d_latch_6 (.in(in[5]), .load(and_1_out), .out(out[5]));  // open: not_out
  d_latch d_latch_7 (.in(in[6]), .load(and_1_out), .out(out[6]));  // open: not_out
  d_latch d_latch_8 (.in(in[7]), .load(and_1_out), .out(out[7]));  // open: not_out

  // Notes on the sheet:
  //   clk = global clock
  //   if wr ^ clk:
  //   else:
  //   wr = write input to reg
  //   out(t)=in(t)
  //   out(t)=out(t-1)
  //   clk ^ wr
endmodule

module _4_bit_reg (
  input  clk,
  input  wr,
  input  [3:0] in,
  output [3:0] out
);

  wire and_1_out;

  \and  and_1 (.a(clk), .b(wr), .out(and_1_out));
  d_latch d_latch_1 (.in(in[0]), .load(and_1_out), .out(out[0]));  // open: not_out
  d_latch d_latch_2 (.in(in[1]), .load(and_1_out), .out(out[1]));  // open: not_out
  d_latch d_latch_3 (.in(in[2]), .load(and_1_out), .out(out[2]));  // open: not_out
  d_latch d_latch_4 (.in(in[3]), .load(and_1_out), .out(out[3]));  // open: not_out

  // Notes on the sheet:
  //   if wr & clk:
  //   out(t)=in(t)
  //   else:
  //   out(t)=out(t-1)
  //   clk & wr
endmodule

module ram4 (
  input  [1:0] idx,
  input  wr,
  input  clk,
  input  [3:0] in,
  output [3:0] out
);

  wire n1_4_1_bit_mux_1_out_0, n1_4_1_bit_mux_1_out_1, n1_4_1_bit_mux_1_out_2, n1_4_1_bit_mux_1_out_3;
  wire [3:0] n1_4_4_bit_mux_1_out_0, n1_4_4_bit_mux_1_out_1, n1_4_4_bit_mux_1_out_2, n1_4_4_bit_mux_1_out_3,
       n4_bit_reg_1_out, n4_bit_reg_2_out, n4_bit_reg_3_out, n4_bit_reg_4_out;

  _1_4_1_bit_mux u_1_4_1_bit_mux_1 (
    .idx(idx), .in(wr), .out_0(n1_4_1_bit_mux_1_out_0), .out_1(n1_4_1_bit_mux_1_out_1),
    .out_2(n1_4_1_bit_mux_1_out_2), .out_3(n1_4_1_bit_mux_1_out_3));
  _1_4_4_bit_mux u_1_4_4_bit_mux_1 (
    .idx(idx), .in(in), .out_0(n1_4_4_bit_mux_1_out_0), .out_1(n1_4_4_bit_mux_1_out_1),
    .out_2(n1_4_4_bit_mux_1_out_2), .out_3(n1_4_4_bit_mux_1_out_3));
  _4_bit_reg u_4_bit_reg_1 (
    .clk(clk), .wr(n1_4_1_bit_mux_1_out_0), .in(n1_4_4_bit_mux_1_out_0), .out(n4_bit_reg_1_out));
  _4_bit_reg u_4_bit_reg_2 (
    .clk(clk), .wr(n1_4_1_bit_mux_1_out_1), .in(n1_4_4_bit_mux_1_out_1), .out(n4_bit_reg_2_out));
  _4_bit_reg u_4_bit_reg_3 (
    .clk(clk), .wr(n1_4_1_bit_mux_1_out_2), .in(n1_4_4_bit_mux_1_out_2), .out(n4_bit_reg_3_out));
  _4_bit_reg u_4_bit_reg_4 (
    .clk(clk), .wr(n1_4_1_bit_mux_1_out_3), .in(n1_4_4_bit_mux_1_out_3), .out(n4_bit_reg_4_out));
  _4_1_4_bit_mux u_4_1_4_bit_mux_1 (
    .idx(idx), .in_0(n4_bit_reg_1_out), .in_1(n4_bit_reg_2_out), .in_2(n4_bit_reg_3_out),
    .in_3(n4_bit_reg_4_out), .out(out));

  // Notes on the sheet:
  //   size: n=4
  //   width: m=4
  //   LOGIC:
  //   if clk & wr[i]:
  //   out(t) = reg[i](t)
  //   2-bit index (max 4 addresses)
  //   1 4-bit input
  //   reg[i](t) = in(t)
  //   note: output is instantly read from i'th register, not synced with clk.
  //   n=4 registers
  //   each m=4 bits
  //   1 4-bit output
endmodule

module _2_bit_counter (
  input  inc,
  input  clk,
  input  en,
  output [1:0] out
);

  wire and_1_out, and_2_out, and_3_out, and_4_out, j_k_ff_1_q, j_k_ff_1_qn, j_k_ff_2_q, j_k_ff_2_qn,
       not_1_output;

  \not  not_1 (.\input (inc), .\output (not_1_output));
  J_K_Flip_Flop j_k_ff_1 (.J(en), .clk(clk), .K(en), .Q(j_k_ff_1_q), .Qn(j_k_ff_1_qn));  // open: preset, en, reset
  \and  and_1 (.a(not_1_output), .b(j_k_ff_1_q), .out(and_1_out));
  \and  and_2 (.a(inc), .b(j_k_ff_1_qn), .out(and_2_out));
  \or  or_1 (.a(and_1_out), .b(and_2_out), .out(out[0]));
  J_K_Flip_Flop j_k_ff_2 (
    .J(en), .clk(j_k_ff_1_q), .K(en), .Q(j_k_ff_2_q), .Qn(j_k_ff_2_qn));  // open: preset, en, reset
  \and  and_3 (.a(not_1_output), .b(j_k_ff_2_q), .out(and_3_out));
  \or  or_2 (.a(and_3_out), .b(and_4_out), .out(out[1]));
  \and  and_4 (.a(inc), .b(j_k_ff_2_qn), .out(and_4_out));
endmodule

module _4_bit_counter (
  input  inc,
  input  clk,
  input  en,
  output [3:0] out
);

  wire [3:0] j_k_ff_1_q, j_k_ff_1_qn;

  J_K_Flip_Flop j_k_ff_1 (
    .J(en), .clk(clk), .K(en), .Q(j_k_ff_1_q[0]), .Qn(j_k_ff_1_qn[0]));  // open: preset, en, reset
  J_K_Flip_Flop j_k_ff_2 (
    .J(en), .clk(j_k_ff_1_q[0]), .K(en), .Q(j_k_ff_1_q[1]), .Qn(j_k_ff_1_qn[1]));  // open: preset, en, reset
  J_K_Flip_Flop j_k_ff_3 (
    .J(en), .clk(j_k_ff_1_q[1]), .K(en), .Q(j_k_ff_1_q[2]), .Qn(j_k_ff_1_qn[2]));  // open: preset, en, reset
  J_K_Flip_Flop j_k_ff_4 (
    .J(en), .clk(j_k_ff_1_q[2]), .K(en), .Q(j_k_ff_1_q[3]), .Qn(j_k_ff_1_qn[3]));  // open: preset, en, reset
  _2_1_4_bit_mux u_2_1_4_bit_mux_1 (.idx(inc), .in_0(j_k_ff_1_q), .in_1(j_k_ff_1_qn), .out(out));
endmodule
